# Fritzing sketch MeteoStation (saved by Fritzing 0.9.3b)
breadboards: 1

parts:
  Part1 = Arduino Uno (Rev3)
  BMP180 = Barometric Pressure Sensor - BMP180 Breakout (GY-68)
  LCD1 = LCD screen
  R2 = Resistor [tolerance=±5% resistance=220 package="0402 [SMD]"]
  R3 = Resistor [tolerance=±5% resistance=220 package="0402 [SMD]"]
  R1 = Resistor [tolerance=±5% resistance=1k package="0402 [SMD]"]
  AM2303 = Humidity and Temperature Sensor RHT03

nets:
  N1: Part1.A4/SDA, BMP180.SDA
  N2: Part1.A5/SCL, BMP180.SCL
  N3: Part1.D9_PWM, R1.Pin_1, AM2303.Data-signal
  N4: Part1.D11_PWM/MOSI, LCD1.E
  N5: Part1.D12/MISO, LCD1.RS
  N6: Part1.D2, LCD1.DB7
  N7: Part1.D3_PWM, LCD1.DB6
  N8: Part1.D4, LCD1.DB5
  N9: Part1.D5_PWM, LCD1.DB4
  VCC: Part1.5V, BMP180.VCC, LCD1.VDD, R3.Pin_0, R1.Pin_0, AM2303.Vcc
  GND: Part1.GND, BMP180.GND, LCD1.VSS, LCD1.R/W, LCD1.LED-, R2.Pin_0, AM2303.GND_2
  N10: LCD1.V0, R2.Pin_1
  N11: LCD1.LED+, R3.Pin_1
